# Fritzing sketch SA_v01 (saved by Fritzing 0.8.0b)
breadboards: 1

parts:
  IC1 = IC, DIP package, 8 pins [chip_label=IC]
  VCC1 = Battery block 9V
  SPKR1 = Loudspeaker
  TRRS1 = Audio Jack (TRRS) 3.5mm [part_number="LUMBERG JEITA RC-5325A" package="RC-5325A [SMD]"]
  C4 = Ceramic Capacitor [capacitance=47µF package="0603 [SMD, multilayer]"]
  C3 = Ceramic Capacitor [capacitance=47µF package="0603 [SMD, multilayer]"]

nets:
  N1: IC1.pin1, IC1.pin8
  N2: IC1.pin2, IC1.pin4, VCC1.-, SPKR1.pin1, TRRS1.SLEEVE, C3.0
  N3: IC1.pin3, TRRS1.TIP, TRRS1.RING1
  N4: IC1.pin5, C4.0
  N5: IC1.pin6, VCC1.+
  N6: IC1.pin7, C3.1
  N7: SPKR1.pin2, C4.1
